# Fritzing sketch Testbed v2 (saved by Fritzing 1.0.5)
circuit board: 14.0468cm x 9.87422cm
breadboards: 1

parts:
  A1 = 4in spi lcd display
  M1 = ESP32-S3-DevKitC-1-N8R8-v1 [part_number=ESP32-S3-DevKitC-1-N8R8-v1]
  OPT_ENC = Sharp PC817 [package=THT]
  ALT = Resistor [tolerance=±5% resistance=10k package="1206 [SMD]"]
  FUEL = Resistor [tolerance=±5% resistance=10k package="1206 [SMD]"]
  TEMP = Resistor [tolerance=±5% resistance=10k package="1206 [SMD]"]
  M3 = RioRand LM2596
  JP1 = M16 [package=1x16_machine-pin-header_lock.004]
  D1 = Zener Diode [part_number=1N4732A breakdown_voltage=3.6V package="300 mil [THT]"]
  C2 = Ceramic Capacitor [capacitance=1µF voltage=35V package="0603 [SMD, multilayer]"]
  OIL1 = Resistor [tolerance=±5% resistance=10k package="1206 [SMD]"]
  C3 = Ceramic Capacitor [capacitance=1µF voltage=35V package="0603 [SMD, multilayer]"]
  D3 = Zener Diode [part_number=1N4732A breakdown_voltage=3.6V package="300 mil [THT]"]
  C1 = Ceramic Capacitor [capacitance=1µF voltage=35V package="0603 [SMD, multilayer]"]
  D2 = Zener Diode [part_number=1N4732A breakdown_voltage=3.6V package="300 mil [THT]"]
  LT_SIG = Resistor [tolerance=±5% resistance=10k package="1206 [SMD]"]
  C4 = Ceramic Capacitor [capacitance=1µF voltage=35V package="0603 [SMD, multilayer]"]
  D4 = Zener Diode [part_number=1N4732A breakdown_voltage=3.6V package="300 mil [THT]"]
  RT_SIG = Resistor [tolerance=±5% resistance=10k package="1206 [SMD]"]
  C5 = Ceramic Capacitor [capacitance=1µF voltage=35V package="0603 [SMD, multilayer]"]
  D5 = Zener Diode [part_number=1N4732A breakdown_voltage=3.6V package="300 mil [THT]"]
  TAIL_LTS = Resistor [tolerance=±5% resistance=10k package="1206 [SMD]"]
  C6 = Ceramic Capacitor [capacitance=1µF voltage=35V package="0603 [SMD, multilayer]"]
  D6 = Zener Diode [part_number=1N4732A breakdown_voltage=3.6V package="300 mil [THT]"]
  MAIN = Resistor [tolerance=±5% resistance=10k package="1206 [SMD]"]
  C7 = Ceramic Capacitor [capacitance=1µF voltage=35V package="0603 [SMD, multilayer]"]
  D7 = Zener Diode [part_number=1N4732A breakdown_voltage=3.6V package="300 mil [THT]"]
  ALT_2 = Resistor [tolerance=±5% resistance=10k package="1206 [SMD]"]
  C10 = Ceramic Capacitor [capacitance=1µF voltage=35V package="0603 [SMD, multilayer]"]
  D10 = Zener Diode [part_number=1N4732A breakdown_voltage=3.6V package="300 mil [THT]"]
  BAT = Battery Holders [package=battery-aaa]
  TEMP_2 = Temperature Sensor (Thermistor) [thermistor_type=NTC package=THT]
  R2 = Resistor [tolerance=±5% resistance=10k package="1206 [SMD]"]
  VM1 = Multimeter (DC Voltage)
  R3 = Resistor [tolerance=±5% resistance=47k package="1206 [SMD]"]
  C9 = Ceramic Capacitor [capacitance=100nF voltage=35V package="0603 [SMD, multilayer]"]
  D9 = Zener Diode [part_number=1N4732A breakdown_voltage=3.6V package="300 mil [THT]"]
  BAT1 = Battery Holders [package=battery-aaa]
  VM2 = Multimeter (DC Voltage)
  R4 = Resistor [tolerance=±5% resistance=10k package="1206 [SMD]"]

nets:
  N1: A1.Pin_1, M1.pin_1, M1.pin_2, M3.Pin_3, ALT_2.Pin_0
  N2: A1.Pin_2, M1.pin_22, M1.pin_44, OPT_ENC.Pin_2, OPT_ENC.Pin_3, FUEL.Pin_1, TEMP.Pin_1, M3.Pin_2, M3.Pin_4, JP1.16, D1.anode, C2.1, OIL1.Pin_0, C3.0, D3.anode, C1.1, D2.anode, LT_SIG.Pin_1, C4.1, D4.anode, RT_SIG.Pin_1, C5.1, D5.anode, TAIL_LTS.Pin_0, C6.0, D6.anode, MAIN.Pin_0, C7.0, D7.anode
  N3: A1.Pin_3, M1.pin_30
  N4: A1.Pin_4, M1.pin_12
  N5: A1.Pin_5, M1.pin_15
  N6: A1.Pin_6, M1.pin_7
  N7: A1.Pin_7, M1.pin_11
  N8: M1.pin_4, FUEL.Pin_0, JP1.14, C2.0, D3.cathode
  N9: M1.pin_5, TEMP.Pin_0, JP1.13, D1.cathode, C1.0
  N10: M1.pin_9, JP1.5, OIL1.Pin_1, C3.1, D2.cathode
  N11: M1.pin_10, JP1.12, LT_SIG.Pin_0, C4.0, D4.cathode
  N12: M1.pin_14, JP1.11, RT_SIG.Pin_0, C5.0, D5.cathode
  N13: M1.pin_40, OPT_ENC.Pin_4, ALT_2.Pin_1
  N14: M1.pin_41, JP1.9, MAIN.Pin_1, C7.1, D7.cathode
  N15: M1.pin_42, JP1.3, TAIL_LTS.Pin_1, C6.1, D6.cathode
  N16: OPT_ENC.Pin_1, ALT.Pin_1
  N17: ALT.Pin_0, JP1.4
  N18: M3.Pin_1, JP1.2
  N19: C10.0, D10.anode, BAT.-, TEMP_2.pin_1, VM1.COM_Probe
  N20: C10.1, D10.cathode, TEMP_2.pin_0, R2.Pin_0, VM1.V_Probe
  N21: BAT.+, R2.Pin_1
  N22: R3.Pin_0, C9.1, D9.cathode, VM2.V_Probe, R4.Pin_1
  N23: R3.Pin_1, BAT1.+
  N24: C9.0, D9.anode, BAT1.-, VM2.COM_Probe, R4.Pin_0

notes:
  GND
  NULL
  FUEL
  TEMP
  LT_SIG
  RT_SIG
  MAIN
  CHARGE
  OIL
  ALT
  TAIL_LIGHTS
  VCC
  This appears to be correct
  This is for ratiometric measurement

custom parts:
  4in spi lcd display: 4.0inch color screen with 320x480 resolution of 65K colors and rich display colors.
  ESP32-S3-DevKitC-1-N8R8-v1: ESP32-S3-DevKitC-1-N8R8-v1 This module is 44pins long (2x22) and 11 pins width.
