# Fritzing sketch Testbed v3 (saved by Fritzing 1.0.5)
circuit board: 31.7876cm x 23.6986cm
breadboards: 2

parts:
  R3 = Resistor [tolerance=±5% resistance=10k package="1206 [SMD]"]
  C2 = Ceramic Capacitor [capacitance=1µF voltage=35V package="0603 [SMD, multilayer]"]
  D2 = Zener Diode [part_number=1N4732A breakdown_voltage=3.6V package="300 mil [THT]"]
  TEMP1 = Temperature Sensor (Thermistor) [thermistor_type=NTC package=THT]
  JP2 = M16 [package=1x16_machine-pin-header_lock.004]
  R9 = Resistor [tolerance=±5% resistance=47k package="1206 [SMD]"]
  R10 = Resistor [tolerance=±5% resistance=10k package="1206 [SMD]"]
  D11 = Zener Diode [part_number=1N4732A breakdown_voltage=3.6V package="300 mil [THT]"]
  R11 = Resistor [tolerance=±5% resistance=10k package="1206 [SMD]"]
  C12 = Ceramic Capacitor [capacitance=1µF voltage=35V package="0603 [SMD, multilayer]"]
  D12 = Zener Diode [part_number=1N4732A breakdown_voltage=3.6V package="300 mil [THT]"]
  TEMP2 = Temperature Sensor (Thermistor) [thermistor_type=NTC package=THT]
  R12 = Resistor [tolerance=±5% resistance=10k package="1206 [SMD]"]
  C13 = Ceramic Capacitor [capacitance=1µF voltage=35V package="0603 [SMD, multilayer]"]
  D13 = Zener Diode [part_number=1N4732A breakdown_voltage=3.6V package="300 mil [THT]"]
  TEMP3 = Temperature Sensor (Thermistor) [thermistor_type=NTC package=THT]
  R13 = Resistor [tolerance=±5% resistance=10k package="1206 [SMD]"]
  C14 = Ceramic Capacitor [capacitance=1µF voltage=35V package="0603 [SMD, multilayer]"]
  D14 = Zener Diode [part_number=1N4732A breakdown_voltage=3.6V package="300 mil [THT]"]
  TEMP4 = Temperature Sensor (Thermistor) [thermistor_type=NTC package=THT]
  R14 = Resistor [tolerance=±5% resistance=10k package="1206 [SMD]"]
  C15 = Ceramic Capacitor [capacitance=1µF voltage=35V package="0603 [SMD, multilayer]"]
  D15 = Zener Diode [part_number=1N4732A breakdown_voltage=3.6V package="300 mil [THT]"]
  TEMP5 = Temperature Sensor (Thermistor) [thermistor_type=NTC package=THT]
  R15 = Resistor [tolerance=±5% resistance=10k package="1206 [SMD]"]
  C16 = Ceramic Capacitor [capacitance=1µF voltage=35V package="0603 [SMD, multilayer]"]
  D16 = Zener Diode [part_number=1N4732A breakdown_voltage=3.6V package="300 mil [THT]"]
  TEMP6 = Temperature Sensor (Thermistor) [thermistor_type=NTC package=THT]
  C17 = Ceramic Capacitor [capacitance=1µF voltage=35V package="0603 [SMD, multilayer]"]
  D17 = Zener Diode [part_number=1N4732A breakdown_voltage=3.6V package="300 mil [THT]"]
  TEMP7 = Temperature Sensor (Thermistor) [thermistor_type=NTC package=THT]
  R16 = Resistor [tolerance=±5% resistance=10k package="1206 [SMD]"]
  R17 = Resistor [tolerance=±5% resistance=10k package="1206 [SMD]"]
  C18 = Ceramic Capacitor [capacitance=1µF voltage=35V package="0603 [SMD, multilayer]"]
  D18 = Zener Diode [part_number=1N4732A breakdown_voltage=3.6V package="300 mil [THT]"]
  TEMP8 = Temperature Sensor (Thermistor) [thermistor_type=NTC package=THT]
  OPT_ENC1 = Sharp PC817 [package=THT]
  ALT1 = Resistor [tolerance=±5% resistance=10k package="1206 [SMD]"]
  M4 = RioRand LM2596
  A2 = 4in spi lcd display
  M5 = ESP32-S3-DevKitC-1-N8R8-v1 [part_number=ESP32-S3-DevKitC-1-N8R8-v1]
  C11 = Ceramic Capacitor [capacitance=100nF voltage=35V package="0603 [SMD, multilayer]"]

nets:
  N1: R3.Pin_0, C2.1, D2.cathode, TEMP1.pin_0, M5.pin_4
  N2: R3.Pin_1, JP2.14
  GND: C2.0, D2.anode, TEMP1.pin_1, JP2.16, R10.Pin_0, D11.anode, C12.0, D12.anode, TEMP2.pin_1, C13.0, D13.anode, TEMP3.pin_1, C14.0, D14.anode, TEMP4.pin_1, C15.0, D15.anode, TEMP5.pin_1, C16.0, D16.anode, TEMP6.pin_1, C17.0, D17.anode, TEMP7.pin_1, C18.0, D18.anode, TEMP8.pin_1, OPT_ENC1.Pin_2, OPT_ENC1.Pin_3, M4.Pin_2, M4.Pin_4, A2.Pin_2, M5.pin_22, M5.pin_23, M5.pin_24, M5.pin_44, C11.0
  N3: JP2.2, R9.Pin_1, M4.Pin_1
  N4: JP2.3, R17.Pin_1
  N5: JP2.4, ALT1.Pin_0
  N6: JP2.5, R16.Pin_1
  N7: JP2.8, R15.Pin_1
  N8: JP2.9, R14.Pin_1
  N9: JP2.11, R13.Pin_1
  N10: JP2.12, R12.Pin_1
  N11: JP2.13, R11.Pin_1
  N12: R9.Pin_0, R10.Pin_1, D11.cathode, M5.pin_20, C11.1
  N13: R11.Pin_0, C12.1, D12.cathode, TEMP2.pin_0, M5.pin_5
  N14: R12.Pin_0, C13.1, D13.cathode, TEMP3.pin_0, M5.pin_10
  N15: R13.Pin_0, C14.1, D14.cathode, TEMP4.pin_0, M5.pin_14
  N16: R14.Pin_0, C15.1, D15.cathode, TEMP5.pin_0, M5.pin_41
  N17: R15.Pin_0, C16.1, D16.cathode, TEMP6.pin_0
  N18: C17.1, D17.cathode, TEMP7.pin_0, R16.Pin_0, M5.pin_9
  N19: R17.Pin_0, C18.1, D18.cathode, TEMP8.pin_0, M5.pin_42
  N20: OPT_ENC1.Pin_1, ALT1.Pin_1
  N21: OPT_ENC1.Pin_4, M5.pin_37
  N22: M4.Pin_3, A2.Pin_1, M5.pin_1, M5.pin_2
  N23: A2.Pin_3, M5.pin_30
  N24: A2.Pin_4, M5.pin_8
  N25: A2.Pin_5, M5.pin_15
  N26: A2.Pin_6, M5.pin_7
  N27: A2.Pin_7, M5.pin_11

notes:
  FUEL
  GND
  MAIN
  RT_SIG
  VCC
  TEMP
  ALT
  NULL
  OIL
  LT_SIG
  TAIL_LIGHTS
  CHARGE
  This is for ratiometric measurement
  TAIL_LTS

custom parts:
  4in spi lcd display: 4.0inch color screen with 320x480 resolution of 65K colors and rich display colors.
  ESP32-S3-DevKitC-1-N8R8-v1: ESP32-S3-DevKitC-1-N8R8-v1 This module is 44pins long (2x22) and 11 pins width.
