# Fritzing sketch Testbed (saved by Fritzing 1.0.5)
circuit board: 14.0468cm x 9.87422cm
breadboards: 1

parts:
  A1 = 4in spi lcd display
  M1 = ESP32-S3-DevKitC-1-N8R8-v1 [part_number=ESP32-S3-DevKitC-1-N8R8-v1]
  OPT_ENC = Sharp PC817 [package=THT]
  RPM1 = Resistor [tolerance=±5% resistance=2.2k package="1206 [SMD]"]
  RPM2 = Resistor [tolerance=±5% resistance=100k package="1206 [SMD]"]
  FUEL = Resistor [tolerance=±5% resistance=220 package="1206 [SMD]"]
  TEMP = Resistor [tolerance=±5% resistance=220 package="1206 [SMD]"]
  OIL = female pin header, 2 pins [form="♀ (female)"]
  OIL_2 = Resistor [tolerance=±5% resistance=1k package="1206 [SMD]"]
  TEMP_2 = female pin header, 2 pins [form="♀ (female)"]
  FUEL_2 = female pin header, 2 pins [form="♀ (female)"]
  RPM = female pin header, 2 pins [form="♀ (female)"]
  M3 = RioRand LM2596

nets:
  N1: A1.Pin_1, A1.Pin_8, M1.pin_21, RPM2.Pin_0, FUEL.Pin_0, TEMP.Pin_0, M3.Pin_3
  N2: A1.Pin_2, M1.pin_22, M1.pin_23, M1.pin_24, M1.pin_44, OPT_ENC.Pin_2, OPT_ENC.Pin_3, OIL_2.Pin_1, M3.Pin_4
  N3: A1.Pin_3, M1.pin_30
  N4: A1.Pin_4, M1.pin_12
  N5: A1.Pin_5, M1.pin_15
  N6: A1.Pin_6, M1.pin_7
  N7: A1.Pin_7, M1.pin_11
  N8: M1.pin_1, M1.pin_2
  N9: M1.pin_17, OPT_ENC.Pin_4, RPM2.Pin_1
  N10: M1.pin_18, TEMP.Pin_1, TEMP_2.pin1
  N11: M1.pin_20, OIL.pin2, OIL_2.Pin_0
  N12: OPT_ENC.Pin_1, RPM1.Pin_1
  N13: RPM1.Pin_0, RPM.pin2
  N14: FUEL.Pin_1, FUEL_2.pin1

custom parts:
  4in spi lcd display: 4.0inch color screen with 320x480 resolution of 65K colors and rich display colors.
  ESP32-S3-DevKitC-1-N8R8-v1: ESP32-S3-DevKitC-1-N8R8-v1 This module is 44pins long (2x22) and 11 pins width.
